// Logisim project CircuitoALU.circ as structural Verilog: 1 circuit, main circuit main
module main (
  input  [15:0] X,
  input  nx,
  input  zx,
  input  no,
  input  [15:0] Y,
  input  F,
  input  zy,
  input  ny,
  output [15:0] out_9,
  output zr,
  output ng
);

  wire or_1_out;
  wire [15:0] adder_1_out, and_1_out, multiplexer_1_out, multiplexer_2_out, multiplexer_3_out,
       multiplexer_4_out, multiplexer_5_out, not_1_out, not_2_out, not_3_out;

  Multiplexer #(.width(16), .enable("false")) multiplexer_1 (
    .in0(X), .in1({16{1'b0}}), .out(multiplexer_1_out), .sel(zx));
  Multiplexer #(.width(16), .enable("false")) multiplexer_2 (
    .in0(Y), .in1({16{1'b0}}), .out(multiplexer_2_out), .sel(zy));
  assign not_1_out = ~multiplexer_1_out;  // NOT_Gate not_1, 16 bits wide
  assign not_2_out = ~multiplexer_2_out;  // NOT_Gate not_2, 16 bits wide
  Multiplexer #(.width(16), .enable("false")) multiplexer_3 (
    .in0(multiplexer_1_out), .in1(not_1_out), .out(multiplexer_3_out), .sel(nx));
  Multiplexer #(.width(16), .enable("false")) multiplexer_4 (
    .in0(multiplexer_2_out), .in1(not_2_out), .out(multiplexer_4_out), .sel(ny));
  Adder #(.width(16)) adder_1 (.a(multiplexer_3_out), .b(multiplexer_4_out), .out(adder_1_out));  // open: cin, cout
  assign and_1_out = multiplexer_3_out & multiplexer_4_out;  // AND_Gate and_1, 16 bits wide
  Multiplexer #(.width(16), .enable("false")) multiplexer_5 (
    .in0(and_1_out), .in1(adder_1_out), .out(multiplexer_5_out), .sel(F));
  assign not_3_out = ~multiplexer_5_out;  // NOT_Gate not_3, 16 bits wide
  Multiplexer #(.width(16), .enable("false")) multiplexer_6 (
    .in0(multiplexer_5_out), .in1(not_3_out), .out({ng, out_9[14:0]}), .sel(no));
  not not_4 (zr, or_1_out);
  or or_1 (or_1_out, out_9[0], out_9[1], out_9[2], out_9[3], out_9[4], out_9[5], out_9[6], out_9[7], out_9[8], out_9[9], out_9[10], out_9[11], out_9[12], out_9[13], out_9[14], ng);

  assign out_9[15] = ng;

  // Notes on the sheet:
  //   ALU
endmodule
